# Fritzing sketch Block_diagram (saved by Fritzing 0.9.9b)

parts:
  Part1 = Arduino Uno (Rev3) - ICSP
  Part2 = BME280
  Grove1 = Grove OLED 128x96
  INA1 = INA219 DC Current Sensor Breakout
  R1 = Resistor [tolerance=±5% power=0.25 resistance=220 package=THT]  # not connected
  R2 = Resistor [tolerance=±5% power=0.25 resistance=220 package=THT]  # not connected
  KY-1 = Keyes Relay [package=THT]
  Mod1 = Raspberry Pi 4B  # not connected
  S1 = SWITCH-MOMENTARY-2 [package=tactile-pth]
  Disp1 = 20mm 8x8 dot matrix column cathode led display with standard pcb pads
  Power_plug1 = Power plug
  IC1 = Rasberry Pi NIOR Camera [chip_label=IC package="DIP (Dual Inline) [THT]"]  # not connected
  DC1 = DC_DC_XL4016 [package=board_screw]
  USBTTL1 = USB A Plug
  USBTTL2 = Micro USB B Plug

nets:
  N1: Part1.A4/SDA, Part2.SDA, Grove1.SDA, INA1.SDA
  N2: Part1.A5/SCL, Part2.SCL, Grove1.SCL, INA1.SCL
  N3: Part1.D10_PWM/SS, S1.2
  N4: Part1.D11_PWM/MOSI, KY-1.signal
  VCC: Part1.5V, Part2.VIN, Grove1.VCC, INA1.VCC
  GND: Part1.GND, Part2.GND, Grove1.GND, INA1.GND, KY-1.ground
  N5: INA1.Vin-2, DC1.IN+
  N6: KY-1.NO, Disp1.pin_13
  N7: Disp1.pin_15, Disp1.pin_16
  N8: Power_plug1.GND, DC1.OUT+
  N9: Power_plug1.VCC, DC1.OUT-
  N10: USBTTL1.usb, USBTTL2.usb

custom parts:
  INA219 DC Current Sensor Breakout: INA DC Current Sensor Breakout
  Keyes Relay: The Keyes 5V relay module is suitable for SCM development, home appliance control. It uses a 5V~12V TIL control signal which can control DC / AC signal.
  Rasberry Pi NIOR Camera: Camera
